# Fritzing sketch Sketch (saved by Fritzing 0.9.3b)

parts:
  LCM1602_IIC3 = LCM1602 IIC [part_number="LCM1602 IIC" chip_label="LCM1602 IIC" package="DIP (Dual Inline) [THT]"]
  LCD2 = LCD screen
  Часть1 = Arduino Uno (Rev3) - ICSP

nets:
  VSS: LCM1602_IIC3.VSS, LCD2.VSS
  VDD: LCM1602_IIC3.VDD, LCD2.VDD
  N1: LCM1602_IIC3.V0, LCD2.V0
  N2: LCM1602_IIC3.RS, LCD2.RS
  N3: LCM1602_IIC3.RW, LCD2.R/W
  N4: LCM1602_IIC3.E, LCD2.E
  N5: LCM1602_IIC3.D0, LCD2.DB0
  N6: LCM1602_IIC3.D1, LCD2.DB1
  N7: LCM1602_IIC3.D2, LCD2.DB2
  N8: LCM1602_IIC3.D3, LCD2.DB3
  N9: LCM1602_IIC3.D4, LCD2.DB4
  N10: LCM1602_IIC3.D5, LCD2.DB5
  N11: LCM1602_IIC3.D6, LCD2.DB6
  N12: LCM1602_IIC3.D7, LCD2.DB7
  N13: LCM1602_IIC3.A, LCD2.LED+
  N14: LCM1602_IIC3.K, LCD2.LED-
  GND: LCM1602_IIC3.GND, Часть1.GND
  VCC: LCM1602_IIC3.VCC, Часть1.5V
  N15: LCM1602_IIC3.SDA, Часть1.A4/SDA
  N16: LCM1602_IIC3.SCL, Часть1.A5/SCL

custom parts:
  LCM1602 IIC: I2C-Module to use a 1602 or 2004 LCD on with the wire.h libory Serial LCD Modul
