# Fritzing sketch Sketch (saved by Fritzing 0.9.3b)
breadboards: 1

parts:
  Часть1 = Arduino Uno (Rev3)
  R1 = Rotary Potentiometer (Large) [maximum_resistance=10kΩ package=THT]
  LED1 = LED - 5mm [color="Red (633nm)" package="5 mm [THT]"]
  R2 = Rotary Potentiometer (Large) [maximum_resistance=10kΩ package=THT]

nets:
  N1: Часть1.A0, R1.wiper
  N2: Часть1.A1, R2.wiper
  N3: Часть1.D5_PWM, LED1.anode
  N4: Часть1.5V, R1.leg1, R2.leg1
  N5: Часть1.GND, R1.leg2, LED1.cathode, R2.leg2
