# Fritzing sketch Sketch (saved by Fritzing 0.9.3b)

parts:
  Часть1 = Arduino Uno (Rev3) - ICSP
  microSD1 = MicroSD Card Module

nets:
  N1: Часть1.D11_PWM/MOSI, microSD1.MOSI
  N2: Часть1.D12/MISO, microSD1.MISO
  N3: Часть1.D13/SCK, microSD1.SCK
  N4: Часть1.D4, microSD1.CS
  5V: Часть1.5V, microSD1.VCC
  GND: Часть1.GND, microSD1.GND
