# Fritzing sketch sketch (saved by Fritzing 0.9.3b)
breadboards: 1

parts:
  LED1 = LED - 5mm [color="Green (555nm)" package="5 mm [THT]"]
  LED4 = LED - 5mm [color="Red (633nm)" package="5 mm [THT]"]
  R1 = Resistor [tolerance=±5% resistance=220 package=THT]
  R2 = Resistor [tolerance=±5% resistance=220 package=THT]
  R3 = Resistor [tolerance=±5% resistance=220 package=THT]
  LED5 = LED - 5mm [color="Yellow (595nm)" package="5 mm [THT]"]
  Часть1 = Arduino Uno (Rev3)

nets:
  N1: LED1.cathode, LED4.cathode, LED5.cathode, Часть1.GND
  N2: LED1.anode, R3.Pin_0
  N3: LED4.anode, R1.Pin_0
  N4: R1.Pin_1, Часть1.D10_PWM/SS
  N5: R2.Pin_0, LED5.anode
  N6: R2.Pin_1, Часть1.D9_PWM
  N7: R3.Pin_1, Часть1.D8
